// Logisim project partial-store.circ as structural Verilog: 1 circuit, main circuit partial_store
module partial_store (
  input  [31:0] Instruction,
  input  [31:0] MemAddress,
  input  [31:0] DataFromReg,
  input  MemWEn,
  output [3:0] MemWriteMask,
  output [31:0] DataToMem
);

  wire [3:0] multiplexer_1_out, multiplexer_2_out, multiplexer_5_out;
  wire [31:0] multiplexer_3_out, multiplexer_4_out;

  Multiplexer #(.select(2), .width(4)) multiplexer_1 (
    .in0(4'b0001), .in1(4'b0010), .in2(4'b0100), .in3(4'b1000), .out(multiplexer_1_out), .sel(MemAddress[1:0]));
  Multiplexer #(.select(2), .width(4)) multiplexer_2 (
    .in0(4'b0011), .in2(4'b1100), .out(multiplexer_2_out), .sel(MemAddress[1:0]));  // open: in1, in3
  Multiplexer #(.select(2), .width(32)) multiplexer_3 (
    .in0({{24{1'b0}}, DataFromReg[7:0]}), .in1({{16{1'b0}}, DataFromReg[7:0], {8{1'b0}}}),
    .in2({{8{1'b0}}, DataFromReg[7:0], {16{1'b0}}}), .in3({DataFromReg[7:0], {24{1'b0}}}),
    .out(multiplexer_3_out), .sel(MemAddress[1:0]));
  Multiplexer #(.select(2), .width(32)) multiplexer_4 (
    .in0({{16{1'b0}}, DataFromReg[15:0]}), .in1({32{1'b0}}), .in2({DataFromReg[15:0], {16{1'b0}}}),
    .in3({32{1'b0}}), .out(multiplexer_4_out), .sel(MemAddress[1:0]));
  Multiplexer #(.select(3), .width(4)) multiplexer_5 (
    .in0(multiplexer_1_out), .in1(multiplexer_2_out), .in2(4'b1111), .in3(4'b0000), .in4(4'b0000),
    .in5(4'b0000), .in6(4'b0000), .in7(4'b0000), .out(multiplexer_5_out), .sel(Instruction[14:12]));
  Multiplexer #(.select(3), .width(32)) multiplexer_6 (
    .in0(multiplexer_3_out), .in1(multiplexer_4_out), .in2(DataFromReg), .in3({32{1'b0}}), .in4({32{1'b0}}),
    .in5({32{1'b0}}), .in6({32{1'b0}}), .in7({32{1'b0}}), .out(DataToMem), .sel(Instruction[14:12]));
  Multiplexer #(.width(4)) multiplexer_7 (.in0(4'b0000), .in1(multiplexer_5_out), .out(MemWriteMask), .sel(MemWEn));

  // Other names for the same wires on the sheet: opcode[6:0] = Instruction[6:0]; rd[4:0] = Instruction[11:7];
  //   func3[2:0] = Instruction[14:12]; rs1[4:0] = Instruction[19:15]; rs2[4:0] = Instruction[24:20];
  //   func7[6:0] = Instruction[31:25]; mux_sel[1:0] = MemAddress[1:0]

  // Notes on the sheet:
  //   INPUTS to your circuit
  //   DECODE
  //   DON'T CHANGE THE LOCATIONS OF THE INPUTS AND OUTPUTS!
  //   sb
  //   sh
  //   OUTPUT from your circuit
endmodule
