// Logisim project regfile.circ as structural Verilog: 1 circuit, main circuit regfile
// en
module regfile (
  input  [4:0] ReadIndex1,
  input  [4:0] ReadIndex2,
  input  [4:0] WriteIndex,
  input  [31:0] WriteData,
  input  RegWEn,
  input  clk,
  output [31:0] ra,
  output [31:0] sp,
  output [31:0] t0,
  output [31:0] t1,
  output [31:0] t2,
  output [31:0] s0,
  output [31:0] s1,
  output [31:0] a0,
  output [31:0] ReadData1,
  output [31:0] ReadData2
);

  wire en1, en2, en3, en4, en5, en6, en7, en8, en9, en10, en11, en12, en13, en14, en15, en16, en17, en18,
       en19, en20, en21, en22, en23, en24, en25, en26, en27, en28, en29, en30, en31;
  wire [31:0] in1, in2, in3, in4, in5, in6, in7, in8, in9, in10, in11, in12, in13, in14, in15, in16, in17,
       in18, in19, in20, in21, in22, in23, in24, in25, in26, in27, in28, in29, in30, in31, out3, out4, out11,
       out12, out13, out14, out15, out16, out17, out18, out19, out20, out21, out22, out23, out24, out25,
       out26, out27, out28, out29, out30, out31;

  Register #(.width(32)) register_1 (.D(in13), .en(en13), .clk(clk), .Q(out13));  // open: clr
  Register #(.width(32)) register_2 (.D(in14), .en(en14), .clk(clk), .Q(out14));  // open: clr
  Register #(.width(32)) register_3 (.D(in15), .en(en15), .clk(clk), .Q(out15));  // open: clr
  Register #(.width(32)) register_4 (.D(in16), .en(en16), .clk(clk), .Q(out16));  // open: clr
  Register #(.width(32)) register_5 (.D(in17), .en(en17), .clk(clk), .Q(out17));  // open: clr
  Register #(.width(32)) register_6 (.D(in18), .en(en18), .clk(clk), .Q(out18));  // open: clr
  Register #(.width(32)) register_7 (.D(in25), .en(en25), .clk(clk), .Q(out25));  // open: clr
  Register #(.width(32)) register_8 (.D(in26), .en(en26), .clk(clk), .Q(out26));  // open: clr
  Register #(.width(32)) register_9 (.D(in27), .en(en27), .clk(clk), .Q(out27));  // open: clr
  Register #(.width(32)) register_10 (.D(in28), .en(en28), .clk(clk), .Q(out28));  // open: clr
  Register #(.width(32)) register_11 (.D(in29), .en(en29), .clk(clk), .Q(out29));  // open: clr
  Register #(.width(32)) register_12 (.D(in30), .en(en30), .clk(clk), .Q(out30));  // open: clr
  Register #(.width(32)) register_13 (.D(in31), .en(en31), .clk(clk), .Q(out31));  // open: clr
  Register #(.width(32)) register_14 (.D(in19), .en(en19), .clk(clk), .Q(out19));  // open: clr
  Register #(.width(32)) register_15 (.D(in20), .en(en20), .clk(clk), .Q(out20));  // open: clr
  Register #(.width(32)) register_16 (.D(in21), .en(en21), .clk(clk), .Q(out21));  // open: clr
  Register #(.width(32)) register_17 (.D(in22), .en(en22), .clk(clk), .Q(out22));  // open: clr
  Register #(.width(32)) register_18 (.D(in23), .en(en23), .clk(clk), .Q(out23));  // open: clr
  Register #(.width(32)) register_19 (.D(in24), .en(en24), .clk(clk), .Q(out24));  // open: clr
  Register #(.width(32)) register_20 (.D(in1), .en(en1), .clk(clk), .Q(ra));  // open: clr
  Register #(.width(32)) register_21 (.D(in2), .en(en2), .clk(clk), .Q(sp));  // open: clr
  Register #(.width(32)) register_22 (.D(in3), .en(en3), .clk(clk), .Q(out3));  // open: clr
  Register #(.width(32)) register_23 (.D(in4), .en(en4), .clk(clk), .Q(out4));  // open: clr
  Register #(.width(32)) register_24 (.D(in5), .en(en5), .clk(clk), .Q(t0));  // open: clr
  Register #(.width(32)) register_25 (.D(in6), .en(en6), .clk(clk), .Q(t1));  // open: clr
  Register #(.width(32)) register_26 (.D(in7), .en(en7), .clk(clk), .Q(t2));  // open: clr
  Register #(.width(32)) register_27 (.D(in8), .en(en8), .clk(clk), .Q(s0));  // open: clr
  Register #(.width(32)) register_28 (.D(in9), .en(en9), .clk(clk), .Q(s1));  // open: clr
  Register #(.width(32)) register_29 (.D(in10), .en(en10), .clk(clk), .Q(a0));  // open: clr
  Register #(.width(32)) register_30 (.D(in11), .en(en11), .clk(clk), .Q(out11));  // open: clr
  Register #(.width(32)) register_31 (.D(in12), .en(en12), .clk(clk), .Q(out12));  // open: clr
  Demultiplexer #(.enable("true"), .select(5), .width(32)) demultiplexer_1 (
    .out1(in1), .out2(in2), .out3(in3), .out4(in4), .out5(in5), .out6(in6), .out7(in7), .out8(in8),
    .out9(in9), .out10(in10), .out11(in11), .out12(in12), .out13(in13), .out14(in14), .out15(in15),
    .out16(in16), .out17(in17), .out18(in18), .out19(in19), .out20(in20), .out21(in21), .out22(in22),
    .out23(in23), .out24(in24), .out25(in25), .out26(in26), .out27(in27), .out28(in28), .out29(in29),
    .out30(in30), .out31(in31), .in(WriteData), .sel(WriteIndex), .en(RegWEn));  // open: out0
  Demultiplexer #(.enable("true"), .select(5)) demultiplexer_2 (
    .out1(en1), .out2(en2), .out3(en3), .out4(en4), .out5(en5), .out6(en6), .out7(en7), .out8(en8),
    .out9(en9), .out10(en10), .out11(en11), .out12(en12), .out13(en13), .out14(en14), .out15(en15),
    .out16(en16), .out17(en17), .out18(en18), .out19(en19), .out20(en20), .out21(en21), .out22(en22),
    .out23(en23), .out24(en24), .out25(en25), .out26(en26), .out27(en27), .out28(en28), .out29(en29),
    .out30(en30), .out31(en31), .in(1'b1), .sel(WriteIndex), .en(RegWEn));  // open: out0
  Multiplexer #(.select(5), .width(32)) multiplexer_1 (
    .in0({32{1'b0}}), .in1(ra), .in2(sp), .in3(out3), .in4(out4), .in5(t0), .in6(t1), .in7(t2), .in8(s0),
    .in9(s1), .in10(a0), .in11(out11), .in12(out12), .in13(out13), .in14(out14), .in15(out15), .in16(out16),
    .in17(out17), .in18(out18), .in19(out19), .in20(out20), .in21(out21), .in22(out22), .in23(out23),
    .in24(out24), .in25(out25), .in26(out26), .in27(out27), .in28(out28), .in29(out29), .in30(out30),
    .in31(out31), .out(ReadData1), .sel(ReadIndex1));
  Multiplexer #(.select(5), .width(32)) multiplexer_2 (
    .in0({32{1'b0}}), .in1(ra), .in2(sp), .in3(out3), .in4(out4), .in5(t0), .in6(t1), .in7(t2), .in8(s0),
    .in9(s1), .in10(a0), .in11(out11), .in12(out12), .in13(out13), .in14(out14), .in15(out15), .in16(out16),
    .in17(out17), .in18(out18), .in19(out19), .in20(out20), .in21(out21), .in22(out22), .in23(out23),
    .in24(out24), .in25(out25), .in26(out26), .in27(out27), .in28(out28), .in29(out29), .in30(out30),
    .in31(out31), .out(ReadData2), .sel(ReadIndex2));

  // Notes on the sheet:
  //   INPUTS to your circuit
  //   DON'T CHANGE THE LOCATIONS OF THE INPUTS AND OUTPUTS!
  //   These are DEBUG/TEST outputs from your circuit.
  //   OUTPUTS from your circuit
endmodule
